// Logisim project real_alu.circ as structural Verilog: 8 circuits, main circuit main
module main (
);


  // Notes on the sheet:
  //   REAL_ALU
endmodule

module Logic_Unit (
  input  [7:0] inA,
  input  Sel2,
  input  Sel1,
  input  Sel0,
  input  [7:0] inB,
  output [7:0] aluOut,
  output OF
);

  wire dxshiftinb_1_of, logicdecoder_1_out_4, logicdecoder_1_out_5, logicdecoder_1_out_6,
       logicdecoder_1_out_7, logicdecoder_1_out_8, sxshiftinb_1_of;
  wire [7:0] dxshiftinb_1_aluout, ina_inb_1_aluout, inaorinb_1_aluout, notinb_1_aluout, sxshiftinb_1_aluout;

  inA_inB ina_inb_1 (.inA(inA), .in_2(logicdecoder_1_out_4), .inB(inB), .aluOut(ina_inb_1_aluout));
  inAorinB inaorinb_1 (.in_3(logicdecoder_1_out_5), .inA(inA), .inB(inB), .aluOut(inaorinb_1_aluout));
  LogicDecoder logicdecoder_1 (
    .out_4(logicdecoder_1_out_4), .out_5(logicdecoder_1_out_5), .out_6(logicdecoder_1_out_6),
    .out_7(logicdecoder_1_out_7), .out_8(logicdecoder_1_out_8), .Sel2(Sel2), .Sel1(Sel1), .Sel0(Sel0));
  NotinB notinb_1 (.in_2(logicdecoder_1_out_6), .inB(inB), .aluout(notinb_1_aluout));
  assign aluOut = ina_inb_1_aluout | inaorinb_1_aluout | notinb_1_aluout | sxshiftinb_1_aluout | dxshiftinb_1_aluout;  // OR_Gate or_1, 8 bits wide
  SxShiftinB sxshiftinb_1 (.inB(inB), .in_2(logicdecoder_1_out_7), .OF(sxshiftinb_1_of), .aluOut(sxshiftinb_1_aluout));
  DxshiftinB dxshiftinb_1 (.inB(inB), .OF(dxshiftinb_1_of), .aluOut(dxshiftinb_1_aluout), .in_2(logicdecoder_1_out_8));
  or or_2 (OF, sxshiftinb_1_of, dxshiftinb_1_of);
endmodule

module inA_inB (
  input  [7:0] inA,
  input  in_2,
  input  [7:0] inB,
  output [7:0] aluOut
);

  wire [7:0] bit_extender_1_out;

  assign bit_extender_1_out = {{7{in_2}}, in_2};  // Bit_Extender bit_extender_1
  assign aluOut = inA & bit_extender_1_out & inB;  // AND_Gate and_1, 8 bits wide
endmodule

module inAorinB (
  input  [7:0] inA,
  input  [7:0] inB,
  input  in_3,
  output [7:0] aluOut
);

  wire [7:0] bit_extender_1_out, or_1_out;

  assign bit_extender_1_out = {{7{in_3}}, in_3};  // Bit_Extender bit_extender_1
  assign or_1_out = inA | inB;  // OR_Gate or_1, 8 bits wide
  assign aluOut = bit_extender_1_out & or_1_out;  // AND_Gate and_1, 8 bits wide
endmodule

module NotinB (
  input  [7:0] inB,
  input  in_2,
  output [7:0] aluout
);

  wire [7:0] bit_extender_1_out, not_1_out;

  assign bit_extender_1_out = {{7{in_2}}, in_2};  // Bit_Extender bit_extender_1
  assign not_1_out = ~inB;  // NOT_Gate not_1, 8 bits wide
  assign aluout = bit_extender_1_out & not_1_out;  // AND_Gate and_1, 8 bits wide
endmodule

module SxShiftinB (
  input  [7:0] inB,
  input  in_2,
  output OF,
  output [7:0] aluOut
);

  wire [6:0] bit_extender_1_out;

  and and_1 (OF, in_2, inB[7]);
  assign aluOut[7:1] = inB[6:0] & bit_extender_1_out;  // AND_Gate and_2, 7 bits wide
  assign bit_extender_1_out = {{6{in_2}}, in_2};  // Bit_Extender bit_extender_1

  assign aluOut[0] = 1'b0;
endmodule

module DxshiftinB (
  input  [7:0] inB,
  input  in_2,
  output OF,
  output [7:0] aluOut
);

  wire [6:0] bit_extender_1_out;

  assign bit_extender_1_out = {{6{in_2}}, in_2};  // Bit_Extender bit_extender_1
  and and_1 (OF, in_2, inB[0]);
  assign aluOut[6:0] = inB[7:1] & bit_extender_1_out;  // AND_Gate and_2, 7 bits wide

  assign aluOut[7] = 1'b0;
endmodule

module LogicDecoder (
  input  Sel2,
  input  Sel1,
  input  Sel0,
  output out_4,
  output out_5,
  output out_6,
  output out_7,
  output out_8
);

  wire not_1_out, not_2_out, not_3_out;

  not not_1 (not_1_out, Sel2);
  not not_2 (not_2_out, Sel0);
  not not_3 (not_3_out, Sel1);
  and and_1 (out_4, not_1_out, not_3_out, not_2_out);
  and and_2 (out_5, not_1_out, not_3_out, Sel0);
  and and_3 (out_6, not_1_out, Sel1, not_2_out);
  and and_4 (out_7, not_1_out, Sel1, Sel0);
  and and_5 (out_8, Sel2, not_3_out, not_2_out);
endmodule
